# Fritzing sketch Dht11+Bluetooth+MIT App Inventor (saved by Fritzing 0.9.3b)
breadboards: 1

parts:
  Parça1 = Arduino Uno (Rev3)
  Parça2 = Bluetooth HC-06 Macho
  RHT1 = Humidity and Temperature Sensor RHT03
  R1 = Resistor [tolerance=±5% resistance=1k package=THT]
  R2 = Resistor [tolerance=±5% resistance=1k package=THT]
  R3 = Resistor [tolerance=±5% resistance=1k package=THT]

nets:
  GND: Parça1.GND, Parça2.GND, RHT1.GND_1, R2.Pin_1
  N1: Parça1.D0/RX, Parça2.TXD
  N2: Parça1.D1/TX, R3.Pin_0
  N3: Parça1.D3_PWM, RHT1.Data-signal
  VCC: Parça1.5V, Parça2.VCC, RHT1.Vcc
  N4: Parça2.RXD, R1.Pin_1
  N5: R1.Pin_0, R3.Pin_1

notes:
  Arduino'ya yazılım gönderildiğinde bluetooth modülünden gelen (TX) ve ard. RX pinine giren bağlantı kablosu çıkarılmalıdır.
